# Fritzing sketch FritzingSchematicDesign (saved by Fritzing 0.9.3b)
perfboards: 1

parts:
  Part1 = Arduino GSM Shield
  Part2 = Arduino Uno (Rev3) - ICSP
  U1 = LCD-16X2 [package=lcd-16x2_noholes]
  KY-1 = Keyes Relay [package=THT]
  Part3 = Adafruit I2C+SPI LCD Backpack [part_number="Adafruit #292"]
  BAT1 = BC9VPC [package=bc9vpc]
  LED1 = LED - 3mm [color="Red (633nm)" package="3 mm [THT]"]

nets:
  N1: Part1.DSM_RX_D2, Part2.D1/TX
  N2: Part1.DSM_TX_D3, Part2.D0/RX
  VSS: U1.VSS, U1.R_W, Part3.GND
  VDD: U1.VDD, U1.A, Part3.VCC
  N3: U1.VO, Part3.CONTRAST
  N4: U1.RS, Part3.RS
  N5: U1.E, Part3.E
  N6: U1.DB0, Part3.DB0
  N7: U1.DB1, Part3.DB1
  N8: U1.DB2, Part3.DB2
  N9: U1.DB3, Part3.DB3
  N10: U1.DB4, Part3.DB4
  N11: U1.DB5, Part3.DB5
  N12: U1.DB6, Part3.DB6
  N13: U1.DB7, Part3.DB7
  N14: U1.K, Part3.LEDK
  N15: KY-1.NO, LED1.cathode
  N16: BAT1.V-, LED1.anode

custom parts:
  Keyes Relay: The Keyes 5V relay module is suitable for SCM development, home appliance control. It uses a 5V~12V TIL control signal which can control DC / AC signal.
  Adafruit I2C+SPI LCD Backpack: LCD backpacks reduce the number of pins needed to connect to an LCD. LCDs are a fun and easy way to have your microcontroller project talk back to you. Character LCDs are common, and easy to get, available in tons of colors and sizes. We've written tutorials on using character LCDs with an Arduino (or similar microcontroller) but find that the number of pins necessary to control the LCD can be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
